// Logisim project 2_3.circ as structural Verilog
module l3z3 (
  input  x3,
  input  x2,
  input  x1,
  output y7,
  output y6,
  output y5,
  output y4,
  output y3,
  output y2,
  output y1
);

  wire and_1_out, and_3_out, and_4_out, and_5_out, or_2_out;

  and and_1 (and_1_out, x3, x2);
  and and_2 (y6, x3, x2);
  and and_3 (and_3_out, x3, x1);
  and and_4 (and_4_out, x3, x2);
  and and_5 (and_5_out, x2, x1);
  or or_1 (y2, x2, x3);
  or or_2 (or_2_out, x1, x2);
  and and_6 (y7, and_1_out, x1);
  or or_3 (y5, and_3_out, and_4_out);
  or or_4 (y3, and_5_out, x3);
  or or_5 (y1, or_2_out, x3);

  assign y4 = x3;
endmodule

module l3z2 (
  input  x4,
  input  x3,
  input  x2,
  input  x1,
  output y4,
  output y3,
  output y2,
  output y1
);

  wire and_1_out, and_2_out, or_1_out, or_2_out, xor_1_out, xor_3_out;

  or or_1 (or_1_out, x2, x1);
  and and_1 (and_1_out, x2, x1);
  xor xor_1 (xor_1_out, x3, or_1_out);
  and and_2 (and_2_out, and_1_out, x3);
  or or_2 (or_2_out, x3, and_1_out);
  xor xor_2 (y3, x4, and_2_out);
  xor xor_3 (xor_3_out, x4, or_2_out);
  not not_1 (y4, xor_3_out);
  not not_2 (y2, xor_1_out);
  not not_3 (y1, x2);
endmodule
