// Logisim project 1.circ as structural Verilog: 2 circuits, main circuit main
module main (
  input  X3,
  input  X2,
  input  X1,
  output F
);

  wire nand_1_out, nand_2_out, nand_3_out, nand_4_out, nand_5_out, nand_6_out, nand_7_out;

  nand nand_1 (nand_1_out, X3, X3);
  nand nand_2 (nand_2_out, X2, X2);
  nand nand_3 (nand_3_out, nand_1_out, nand_2_out);
  nand nand_4 (nand_4_out, nand_1_out, X1);
  nand nand_5 (nand_5_out, nand_3_out, nand_3_out);
  nand nand_6 (nand_6_out, X2, nand_4_out);
  nand nand_7 (nand_7_out, nand_5_out, X1);
  nand nand_8 (F, nand_7_out, nand_6_out);
endmodule

module test (
);

  wire and_1_out, button_1_out, main_1_f, t_ff_1_q, t_ff_2_q, t_ff_3_q;

  Button button_1 (.out(button_1_out));
  T_Flip_Flop t_ff_1 (.T(1'b1), .clk(button_1_out), .Q(t_ff_1_q));  // open: Qn, reset, preset
  T_Flip_Flop t_ff_2 (.T(t_ff_1_q), .clk(button_1_out), .Q(t_ff_2_q));  // open: Qn, reset, preset
  T_Flip_Flop t_ff_3 (.T(and_1_out), .clk(button_1_out), .Q(t_ff_3_q));  // open: Qn, reset, preset
  and and_1 (and_1_out, t_ff_2_q, t_ff_1_q);
  LED led_1 (.in(main_1_f));
  main main_1 (.X3(t_ff_1_q), .X2(t_ff_2_q), .X1(t_ff_3_q), .F(main_1_f));
endmodule
