// Logisim project 2.circ as structural Verilog: 2 circuits, main circuit main
module main (
  input  C_in,
  input  A1,
  input  A2,
  input  A3,
  input  A4,
  input  B1,
  input  B2,
  input  B3,
  input  B4
);

  wire clock_1_out, summ_1_c_out, summ_1_s, summ_2_c_out, summ_2_s, summ_3_c_out, summ_3_s, summ_4_c_out,
       summ_4_s;

  Clock clock_1 (.out(clock_1_out));
  LED led_1 (.in(clock_1_out));
  summ summ_1 (.A(A1), .B(B1), .C_in(C_in), .S(summ_1_s), .C_out(summ_1_c_out));
  summ summ_2 (.A(A2), .B(B2), .C_in(summ_1_c_out), .S(summ_2_s), .C_out(summ_2_c_out));
  summ summ_3 (.A(A3), .B(B3), .C_in(summ_2_c_out), .S(summ_3_s), .C_out(summ_3_c_out));
  summ summ_4 (.A(A4), .B(B4), .C_in(summ_3_c_out), .S(summ_4_s), .C_out(summ_4_c_out));
  LED S1 (.in(summ_1_s));
  LED S2 (.in(summ_2_s));
  LED S3 (.in(summ_3_s));
  LED S4 (.in(summ_4_s));
  LED C_out (.in(summ_4_c_out));
endmodule

module summ (
  input  A,
  input  B,
  input  C_in,
  output S,
  output C_out
);

  wire nand_1_out, nand_2_out, nand_3_out, nand_4_out, nand_5_out, nand_6_out, nand_8_out;

  nand nand_1 (nand_1_out, A, B);
  nand nand_2 (nand_2_out, A, nand_1_out);
  nand nand_3 (nand_3_out, nand_1_out, B);
  nand nand_4 (nand_4_out, nand_2_out, nand_3_out);
  nand nand_5 (nand_5_out, nand_4_out, C_in);
  nand nand_6 (nand_6_out, nand_4_out, nand_5_out);
  nand nand_7 (S, nand_6_out, nand_8_out);
  nand nand_8 (nand_8_out, nand_5_out, C_in);
  nand nand_9 (C_out, nand_1_out, nand_5_out);
endmodule
