// Logisim project 3.circ as structural Verilog: 1 circuit, main circuit main
module main (
);

  wire and_1_out, and_2_out, and_3_out, and_4_out, C_a_out, C_b_out, t_ff_1_q, t_ff_2_q, t_ff_2_qn, t_ff_3_q,
       t_ff_4_q, t_ff_4_qn, t_ff_5_q, t_ff_6_q, t_ff_6_qn, t_ff_7_q, t_ff_8_q;

  Button C_a (.out(C_a_out));
  Button C_b (.out(C_b_out));
  LED A1 (.in(t_ff_1_q));
  T_Flip_Flop t_ff_1 (.T(1'b1), .clk(C_a_out), .Q(t_ff_1_q));  // open: Qn, reset, preset
  LED B1 (.in(t_ff_2_q));
  T_Flip_Flop t_ff_2 (.T(1'b1), .clk(C_b_out), .Q(t_ff_2_q), .Qn(t_ff_2_qn));  // open: reset, preset
  LED A2 (.in(t_ff_3_q));
  LED A4 (.in(t_ff_5_q));
  T_Flip_Flop t_ff_3 (.T(t_ff_1_q), .clk(C_a_out), .Q(t_ff_3_q));  // open: Qn, reset, preset
  LED B2 (.in(t_ff_4_q));
  LED B4 (.in(t_ff_6_q));
  T_Flip_Flop t_ff_4 (.T(t_ff_2_qn), .clk(C_b_out), .Q(t_ff_4_q), .Qn(t_ff_4_qn));  // open: reset, preset
  LED A8 (.in(t_ff_7_q));
  and and_1 (and_1_out, t_ff_1_q, t_ff_3_q);
  LED B8 (.in(t_ff_8_q));
  and and_2 (and_2_out, t_ff_2_qn, t_ff_4_qn);
  T_Flip_Flop t_ff_5 (.T(and_1_out), .clk(C_a_out), .Q(t_ff_5_q));  // open: Qn, reset, preset
  T_Flip_Flop t_ff_6 (.T(and_2_out), .clk(C_b_out), .Q(t_ff_6_q), .Qn(t_ff_6_qn));  // open: reset, preset
  and and_3 (and_3_out, and_1_out, t_ff_5_q);
  T_Flip_Flop t_ff_7 (.T(and_3_out), .clk(C_a_out), .Q(t_ff_7_q));  // open: Qn, reset, preset
  and and_4 (and_4_out, and_2_out, t_ff_6_qn);
  T_Flip_Flop t_ff_8 (.T(and_4_out), .clk(C_b_out), .Q(t_ff_8_q));  // open: Qn, reset, preset
endmodule
