// Logisim project 4.circ as structural Verilog: 2 circuits, main circuit dec
module main (
);

  wire and_1_out, and_2_out, and_3_out, clock_1_out, dec_1_q0, dec_1_q1, dec_1_q2, dec_1_q3, dec_1_q4,
       dec_1_q5, dec_1_q6, dec_1_q7, dec_1_q8, dec_1_q9, dec_1_q10, dec_1_q11, not_1_out, not_2_out,
       t_ff_1_q, t_ff_2_q, t_ff_3_q, t_ff_4_q;

  T_Flip_Flop t_ff_1 (.T(1'b1), .clk(clock_1_out), .Q(t_ff_1_q), .reset(and_3_out));  // open: Qn, preset
  Clock clock_1 (.out(clock_1_out));
  T_Flip_Flop t_ff_2 (.T(t_ff_1_q), .clk(clock_1_out), .Q(t_ff_2_q), .reset(and_3_out));  // open: Qn, preset
  T_Flip_Flop t_ff_3 (.T(and_1_out), .clk(clock_1_out), .Q(t_ff_3_q), .reset(and_3_out));  // open: Qn, preset
  T_Flip_Flop t_ff_4 (.T(and_2_out), .clk(clock_1_out), .Q(t_ff_4_q), .reset(and_3_out));  // open: Qn, preset
  and and_1 (and_1_out, t_ff_2_q, t_ff_1_q);
  and and_2 (and_2_out, t_ff_3_q, and_1_out);
  not not_1 (not_1_out, t_ff_1_q);
  not not_2 (not_2_out, t_ff_2_q);
  and and_3 (and_3_out, not_1_out, not_2_out, t_ff_3_q, t_ff_4_q);
  LED led_1 (.in(dec_1_q0));
  dec dec_1 (
    .A1(t_ff_1_q), .A2(t_ff_2_q), .A3(t_ff_3_q), .A4(t_ff_4_q), .Q1(dec_1_q1), .Q3(dec_1_q3), .Q5(dec_1_q5),
    .Q7(dec_1_q7), .Q9(dec_1_q9), .Q11(dec_1_q11), .Q0(dec_1_q0), .Q2(dec_1_q2), .Q4(dec_1_q4),
    .Q6(dec_1_q6), .Q8(dec_1_q8), .Q10(dec_1_q10));
  LED led_2 (.in(dec_1_q1));
  LED led_3 (.in(dec_1_q2));
  LED led_4 (.in(dec_1_q3));
  LED led_5 (.in(dec_1_q4));
  LED led_6 (.in(dec_1_q5));
  LED led_7 (.in(dec_1_q6));
  LED led_8 (.in(dec_1_q7));
  LED led_9 (.in(dec_1_q8));
  LED led_10 (.in(dec_1_q9));
  LED led_11 (.in(dec_1_q10));
  LED led_12 (.in(dec_1_q11));
endmodule

module dec (
  input  A1,
  input  A2,
  input  A3,
  input  A4,
  output Q1,
  output Q0,
  output Q3,
  output Q2,
  output Q5,
  output Q4,
  output Q7,
  output Q6,
  output Q9,
  output Q8,
  output Q11,
  output Q10
);

  wire not_1_out, not_2_out, not_3_out, not_4_out;

  not not_1 (not_1_out, A1);
  not not_2 (not_2_out, A2);
  not not_3 (not_3_out, A3);
  not not_4 (not_4_out, A4);
  and and_1 (Q1, A1, not_2_out, not_3_out, not_4_out);
  and and_2 (Q3, A1, A2, not_3_out, not_4_out);
  and and_3 (Q5, A1, not_2_out, A3, not_4_out);
  and and_4 (Q7, A1, A2, A3, not_4_out);
  and and_5 (Q9, A1, not_2_out, not_3_out, A4);
  and and_6 (Q11, A1, A2, not_3_out, A4);
  and and_7 (Q0, not_1_out, not_2_out, not_3_out, not_4_out);
  and and_8 (Q2, not_1_out, A2, not_3_out, not_4_out);
  and and_9 (Q4, not_1_out, not_2_out, A3, not_4_out);
  and and_10 (Q6, not_1_out, A2, A3, not_4_out);
  and and_11 (Q8, not_1_out, not_2_out, not_3_out, A4);
  and and_12 (Q10, not_1_out, A2, not_3_out, A4);
endmodule
