// Logisim project 4w.circ as structural Verilog: 1 circuit, main circuit main
module main (
  input  in_1
);

  wire button_1_out, button_2_out, clock_1_out, d_ff_1_q, d_ff_2_q, d_ff_3_q, d_ff_4_q, d_ff_5_q, d_ff_6_q,
       d_ff_7_q, d_ff_8_q, d_ff_9_q, d_ff_10_q, d_ff_11_q, d_ff_12_q, or_1_out;

  Button button_1 (.out(button_1_out));
  D_Flip_Flop d_ff_1 (
    .D(d_ff_12_q), .clk(clock_1_out), .Q(d_ff_1_q), .preset(button_1_out), .reset(button_2_out));  // open: Qn
  Clock clock_1 (.out(clock_1_out));
  Button button_2 (.out(button_2_out));
  LED led_1 (.in(d_ff_1_q));
  LED led_2 (.in(d_ff_2_q));
  LED led_3 (.in(d_ff_3_q));
  or or_1 (or_1_out, d_ff_1_q, d_ff_12_q);
  D_Flip_Flop d_ff_2 (.D(or_1_out), .clk(clock_1_out), .Q(d_ff_2_q), .reset(button_2_out));  // open: Qn, preset
  LED led_4 (.in(d_ff_4_q));
  LED led_5 (.in(d_ff_5_q));
  LED led_6 (.in(d_ff_6_q));
  LED led_7 (.in(d_ff_7_q));
  D_Flip_Flop d_ff_3 (.D(d_ff_2_q), .clk(clock_1_out), .Q(d_ff_3_q), .reset(button_2_out));  // open: Qn, preset
  LED led_8 (.in(d_ff_8_q));
  LED led_9 (.in(d_ff_9_q));
  LED led_10 (.in(d_ff_10_q));
  LED led_11 (.in(d_ff_11_q));
  D_Flip_Flop d_ff_4 (.D(d_ff_3_q), .clk(clock_1_out), .Q(d_ff_4_q), .reset(button_2_out));  // open: Qn, preset
  LED led_12 (.in(d_ff_12_q));
  D_Flip_Flop d_ff_5 (.D(d_ff_4_q), .clk(clock_1_out), .Q(d_ff_5_q), .reset(button_2_out));  // open: Qn, preset
  D_Flip_Flop d_ff_6 (.D(d_ff_5_q), .clk(clock_1_out), .Q(d_ff_6_q), .reset(button_2_out));  // open: Qn, preset
  D_Flip_Flop d_ff_7 (.D(d_ff_6_q), .clk(clock_1_out), .Q(d_ff_7_q), .reset(button_2_out));  // open: Qn, preset
  D_Flip_Flop d_ff_8 (.D(d_ff_7_q), .clk(clock_1_out), .Q(d_ff_8_q), .reset(button_2_out));  // open: Qn, preset
  D_Flip_Flop d_ff_9 (.D(d_ff_8_q), .clk(clock_1_out), .Q(d_ff_9_q), .reset(button_2_out));  // open: Qn, preset
  D_Flip_Flop d_ff_10 (.D(d_ff_9_q), .clk(clock_1_out), .Q(d_ff_10_q), .reset(button_2_out));  // open: Qn, preset
  D_Flip_Flop d_ff_11 (.D(d_ff_10_q), .clk(clock_1_out), .Q(d_ff_11_q), .reset(button_2_out));  // open: Qn, preset
  D_Flip_Flop d_ff_12 (.D(d_ff_11_q), .clk(clock_1_out), .Q(d_ff_12_q), .reset(button_2_out));  // open: Qn, preset
endmodule
