// Logisim project 5.circ as structural Verilog: 2 circuits, main circuit main
module main (
  input  A1,
  input  A2,
  input  A4,
  input  A8,
  output a,
  output b,
  output c,
  output d,
  output e,
  output f,
  output g
);

  wire and_1_out, and_2_out, and_3_out, and_4_out, and_5_out, and_6_out, and_7_out, and_8_out, and_9_out,
       not_1_out, not_2_out, not_3_out, not_4_out;

  not not_1 (not_1_out, A1);
  not not_2 (not_2_out, A2);
  not not_3 (not_3_out, A4);
  not not_4 (not_4_out, A8);
  and and_1 (and_1_out, not_1_out, not_2_out, not_3_out, not_4_out);
  and and_2 (and_2_out, A1, not_2_out, not_3_out, not_4_out);
  and and_3 (and_3_out, not_1_out, A2, not_3_out, not_4_out);
  and and_4 (and_4_out, A1, A2, not_3_out, not_4_out);
  and and_5 (and_5_out, not_1_out, not_2_out, A4, not_4_out);
  and and_6 (and_6_out, A1, not_2_out, A4, not_4_out);
  and and_7 (and_7_out, not_1_out, A2, A4, not_4_out);
  and and_8 (and_8_out, A1, A2, A4, not_4_out);
  and and_9 (and_9_out, A1, not_2_out, not_3_out, A8);
  nor nor_1 (a, and_2_out, and_5_out);
  nor nor_2 (b, and_6_out, and_7_out);
  not not_5 (c, and_3_out);
  nor nor_3 (d, and_2_out, and_5_out, and_8_out);
  nor nor_4 (e, and_2_out, and_4_out, and_5_out, and_6_out, and_8_out, and_9_out);
  nor nor_5 (f, and_2_out, and_3_out, and_4_out, and_8_out);
  nor nor_6 (g, and_1_out, and_2_out, and_8_out);
endmodule

module test (
);

  wire and_1_out, and_2_out, and_3_out, button_1_out, main_1_a, main_1_b, main_1_c, main_1_d, main_1_e,
       main_1_f, main_1_g, not_1_out, not_2_out, t_ff_1_q, t_ff_2_q, t_ff_3_q, t_ff_4_q;

  Button button_1 (.out(button_1_out));
  T_Flip_Flop t_ff_1 (.T(1'b1), .clk(button_1_out), .Q(t_ff_1_q), .reset(and_3_out));  // open: Qn, preset
  T_Flip_Flop t_ff_2 (.T(t_ff_1_q), .clk(button_1_out), .Q(t_ff_2_q), .reset(and_3_out));  // open: Qn, preset
  T_Flip_Flop t_ff_3 (.T(and_1_out), .clk(button_1_out), .Q(t_ff_3_q), .reset(and_3_out));  // open: Qn, preset
  T_Flip_Flop t_ff_4 (.T(and_2_out), .clk(button_1_out), .Q(t_ff_4_q), .reset(and_3_out));  // open: Qn, preset
  and and_1 (and_1_out, t_ff_2_q, t_ff_1_q);
  and and_2 (and_2_out, t_ff_3_q, and_1_out);
  not not_1 (not_1_out, t_ff_1_q);
  not not_2 (not_2_out, t_ff_3_q);
  and and_3 (and_3_out, not_1_out, t_ff_2_q, not_2_out, t_ff_4_q);
  main main_1 (
    .A1(t_ff_1_q), .A2(t_ff_2_q), .A4(t_ff_3_q), .A8(t_ff_4_q), .a(main_1_a), .b(main_1_b), .c(main_1_c),
    .d(main_1_d), .e(main_1_e), .f(main_1_f), .g(main_1_g));
  _7_Segment_Display #(.decimalPoint("false")) u_7_segment_display_1 (
    .g(main_1_g), .f(main_1_f), .a(main_1_a), .b(main_1_b), .e(main_1_e), .d(main_1_d), .c(main_1_c));
endmodule
