// Logisim project 6.circ as structural Verilog: 2 circuits, main circuit main
module main (
  input  D4,
  input  C,
  input  R,
  output Q4,
  output Q3,
  output Q2,
  output Q1,
  output N
);

  D_Flip_Flop d_ff_1 (.D(D4), .clk(C), .Q(Q4), .reset(R));  // open: Qn, preset
  D_Flip_Flop d_ff_2 (.D(Q4), .clk(C), .Q(Q3), .reset(R));  // open: Qn, preset
  D_Flip_Flop d_ff_3 (.D(Q3), .clk(C), .Q(Q2), .reset(R));  // open: Qn, preset
  D_Flip_Flop d_ff_4 (.D(Q2), .clk(C), .Q(N), .reset(R));  // open: Qn, preset

  assign Q1 = N;
endmodule

module test (
  input  in_1
);

  wire button_1_out, button_2_out, main_1_n, main_1_q1, main_1_q2, main_1_q3, main_1_q4, main_2_n, main_2_q1,
       main_2_q2, main_2_q3, main_2_q4;

  Button button_1 (.out(button_1_out));
  Button button_2 (.out(button_2_out));
  main main_1 (
    .D4(in_1), .C(button_1_out), .R(button_2_out), .Q4(main_1_q4), .Q3(main_1_q3), .Q2(main_1_q2),
    .Q1(main_1_q1), .N(main_1_n));
  main main_2 (
    .D4(main_1_n), .C(button_1_out), .R(button_2_out), .Q4(main_2_q4), .Q3(main_2_q3), .Q2(main_2_q2),
    .Q1(main_2_q1), .N(main_2_n));
  LED led_1 (.in(main_1_q4));
  LED led_2 (.in(main_1_q3));
  LED led_3 (.in(main_1_q2));
  LED led_4 (.in(main_1_q1));
  LED led_5 (.in(main_2_q4));
  LED led_6 (.in(main_2_q3));
  LED led_7 (.in(main_2_q2));
  LED led_8 (.in(main_2_q1));
  LED led_9 (.in(main_2_n));
endmodule
