// Logisim project 7.circ as structural Verilog
module main (
  input  A1,
  input  A2,
  input  A3,
  input  A4,
  input  A5,
  input  A6,
  input  A7,
  input  A8,
  input  B1,
  input  B2,
  input  B3,
  input  B4,
  input  B5,
  input  B6,
  input  B7,
  input  B8,
  input  C,
  input  S,
  input  R
);
endmodule

module counter0 (
  input  A1,
  input  A2,
  input  A3,
  input  A4,
  input  A5,
  input  A6,
  input  A7,
  input  A8
);

  T_Flip_Flop t_ff_1 ();  // open: T, clk, Q, Qn, reset, preset
endmodule
