// Logisim project 8.circ as structural Verilog: 5 circuits, main circuit main
module main (
  input  [63:0] A,
  input  [63:0] B,
  input  Cin,
  output [63:0] S,
  output Cout
);

  wire cla2_1_g, cla2_1_p, cla2_2_g, cla2_2_p, cla2_3_g, cla2_3_p, cla2_4_g, cla2_4_p, cla_1_c1, cla_1_c2,
       cla_1_c3;
  wire [15:0] pre2_1_g, pre2_1_p, pre2_2_g, pre2_2_p, pre2_3_g, pre2_3_p, pre2_4_g, pre2_4_p;

  pre2 pre2_1 (.A(A[15:0]), .B(B[15:0]), .P(pre2_1_p), .G(pre2_1_g));
  pre2 pre2_2 (.A(A[31:16]), .B(B[31:16]), .P(pre2_2_p), .G(pre2_2_g));
  pre2 pre2_3 (.A(A[47:32]), .B(B[47:32]), .P(pre2_3_p), .G(pre2_3_g));
  pre2 pre2_4 (.A(A[63:48]), .B(B[63:48]), .P(pre2_4_p), .G(pre2_4_g));
  cla2 cla2_1 (.C(Cin), .Pi(pre2_1_p), .Gi(pre2_1_g), .P(cla2_1_p), .G(cla2_1_g), .S(S[15:0]));  // open: C16
  cla2 cla2_2 (.C(cla_1_c1), .Pi(pre2_2_p), .Gi(pre2_2_g), .P(cla2_2_p), .G(cla2_2_g), .S(S[31:16]));  // open: C16
  cla2 cla2_3 (.C(cla_1_c2), .Pi(pre2_3_p), .Gi(pre2_3_g), .P(cla2_3_p), .G(cla2_3_g), .S(S[47:32]));  // open: C16
  cla2 cla2_4 (.C(cla_1_c3), .Pi(pre2_4_p), .Gi(pre2_4_g), .C16(Cout), .P(cla2_4_p), .G(cla2_4_g), .S(S[63:48]));
  cla cla_1 (
    .P0(cla2_1_p), .P1(cla2_2_p), .P2(cla2_3_p), .P3(cla2_4_p), .G0(cla2_1_g), .G1(cla2_2_g), .G2(cla2_3_g),
    .G3(cla2_4_g), .C0(Cin), .C1(cla_1_c1), .C2(cla_1_c2), .C3(cla_1_c3));  // open: G, P, S0, S1, S2, S3, C4
endmodule

module cla (
  input  P0,
  input  P1,
  input  P2,
  input  P3,
  input  G0,
  input  G1,
  input  G2,
  input  G3,
  input  C0,
  output S0,
  output C1,
  output S1,
  output C2,
  output S2,
  output C3,
  output S3,
  output C4,
  output G,
  output P
);

  wire and_1_out, and_2_out, and_3_out, and_4_out, and_5_out, and_6_out, and_7_out, and_8_out, and_9_out,
       and_10_out;

  and and_1 (and_1_out, P0, C0);
  and and_2 (and_2_out, G0, P1);
  and and_3 (and_3_out, P0, P1, C0);
  and and_4 (and_4_out, G1, P2);
  and and_5 (and_5_out, G0, P1, P2);
  and and_6 (and_6_out, P0, P1, P2, C0);
  and and_7 (and_7_out, G2, P3);
  and and_8 (and_8_out, G1, P2, P3);
  and and_9 (and_9_out, G0, P1, P2, P3);
  and and_10 (and_10_out, P0, P1, P2, P3, C0);
  and and_11 (P, P3, P2, P1, P0);
  xor xor_1 (S0, C0, P0);
  or or_1 (C1, G0, and_1_out);
  or or_2 (C2, G1, and_2_out, and_3_out);
  or or_3 (C3, G2, and_5_out, and_4_out, and_6_out);
  or or_4 (C4, G3, and_8_out, and_9_out, and_7_out, and_10_out);
  or or_5 (G, and_7_out, and_9_out, and_8_out, G3);
  xor xor_2 (S1, C1, P1);
  xor xor_3 (S2, C2, P2);
  xor xor_4 (S3, C3, P3);
endmodule

module cla2 (
  input  C,
  input  [15:0] Pi,
  input  [15:0] Gi,
  output [15:0] S,
  output P,
  output G,
  output C16
);

  wire cla_1_g, cla_1_p, cla_2_g, cla_2_p, cla_3_g, cla_3_p, cla_4_g, cla_4_p, cla_5_c1, cla_5_c2, cla_5_c3;

  cla cla_1 (
    .P0(Pi[0]), .P1(Pi[1]), .P2(Pi[2]), .P3(Pi[3]), .G0(Gi[0]), .G1(Gi[1]), .G2(Gi[2]), .G3(Gi[3]), .C0(C),
    .G(cla_1_g), .P(cla_1_p), .S0(S[0]), .S1(S[1]), .S2(S[2]), .S3(S[3]));  // open: C1, C2, C3, C4
  cla cla_2 (
    .P0(Pi[4]), .P1(Pi[5]), .P2(Pi[6]), .P3(Pi[7]), .G0(Gi[4]), .G1(Gi[5]), .G2(Gi[6]), .G3(Gi[7]),
    .C0(cla_5_c1), .G(cla_2_g), .P(cla_2_p), .S0(S[4]), .S1(S[5]), .S2(S[6]), .S3(S[7]));  // open: C1, C2, C3, C4
  cla cla_3 (
    .P0(Pi[8]), .P1(Pi[9]), .P2(Pi[10]), .P3(Pi[11]), .G0(Gi[8]), .G1(Gi[9]), .G2(Gi[10]), .G3(Gi[11]),
    .C0(cla_5_c2), .G(cla_3_g), .P(cla_3_p), .S0(S[8]), .S1(S[9]), .S2(S[10]), .S3(S[11]));  // open: C1, C2, C3, C4
  cla cla_4 (
    .P0(Pi[12]), .P1(Pi[13]), .P2(Pi[14]), .P3(Pi[15]), .G0(Gi[12]), .G1(Gi[13]), .G2(Gi[14]), .G3(Gi[15]),
    .C0(cla_5_c3), .G(cla_4_g), .P(cla_4_p), .S0(S[12]), .S1(S[13]), .S2(S[14]), .S3(S[15]), .C4(C16));  // open: C1, C2, C3
  cla cla_5 (
    .P0(cla_1_p), .P1(cla_2_p), .P2(cla_3_p), .P3(cla_4_p), .G0(cla_1_g), .G1(cla_2_g), .G2(cla_3_g),
    .G3(cla_4_g), .C0(C), .G(G), .P(P), .C1(cla_5_c1), .C2(cla_5_c2), .C3(cla_5_c3));  // open: S0, S1, S2, S3, C4
endmodule

module pre (
  input  A,
  input  B,
  output P,
  output G
);

  xor xor_1 (P, A, B);
  and and_1 (G, A, B);
endmodule

module pre2 (
  input  [15:0] A,
  input  [15:0] B,
  output [15:0] P,
  output [15:0] G
);

  pre pre_1 (.A(A[0]), .B(B[0]), .P(P[0]), .G(G[0]));
  pre pre_2 (.A(A[1]), .B(B[1]), .P(P[1]), .G(G[1]));
  pre pre_3 (.A(A[2]), .B(B[2]), .P(P[2]), .G(G[2]));
  pre pre_4 (.A(A[3]), .B(B[3]), .P(P[3]), .G(G[3]));
  pre pre_5 (.A(A[4]), .B(B[4]), .P(P[4]), .G(G[4]));
  pre pre_6 (.A(A[5]), .B(B[5]), .P(P[5]), .G(G[5]));
  pre pre_7 (.A(A[6]), .B(B[6]), .P(P[6]), .G(G[6]));
  pre pre_8 (.A(A[7]), .B(B[7]), .P(P[7]), .G(G[7]));
  pre pre_9 (.A(A[8]), .B(B[8]), .P(P[8]), .G(G[8]));
  pre pre_10 (.A(A[9]), .B(B[9]), .P(P[9]), .G(G[9]));
  pre pre_11 (.A(A[10]), .B(B[10]), .P(P[10]), .G(G[10]));
  pre pre_12 (.A(A[11]), .B(B[11]), .P(P[11]), .G(G[11]));
  pre pre_13 (.A(A[12]), .B(B[12]), .P(P[12]), .G(G[12]));
  pre pre_14 (.A(A[13]), .B(B[13]), .P(P[13]), .G(G[13]));
  pre pre_15 (.A(A[14]), .B(B[14]), .P(P[14]), .G(G[14]));
  pre pre_16 (.A(A[15]), .B(B[15]), .P(P[15]), .G(G[15]));
endmodule
